# Fritzing sketch MicromouseMotors (saved by Fritzing 0.9.2b)
breadboards: 1

parts:
  IC1 = L293D [package=THT]
  U1 = SN74LS14N [package="DIP14 [THT]"]
  Part1 = Arduino Pro Mini v13
  IC2 = L293D [package=THT]
  Part2 = Arduino Pro Mini v13
  M1 = DC Motor
  Motor_Power_Source = Battery block 9V
  IC3 = L293D [package=THT]
  Part3 = Arduino Pro Mini v13
  M2 = DC Motor
  Motor_Power_Source1 = Battery block 9V
  U2 = SN74LS14N [package="DIP14 [THT]"]

nets:
  N1: IC1.Enable_1, Part1.D5_PWM
  N2: IC1.In_1, U1.1A, Part1.D4
  N3: IC1.In_2, U1.1Y
  N4: IC1.Enable_2, Part1.D6_PWM
  N5: IC1.In_3, U1.2A, Part1.D7
  N6: IC1.In_4, U1.2Y
  N7: IC2.Enable_1, Part2.D9_PWM
  N8: IC2.In_1, Part2.D8
  N9: IC2.Out_1_(_Controlled_by_Enable_1_), M1.pin_1
  N10: IC2.Out_2_(_Controlled_by_Enable_1_), M1.pin_2
  N11: IC2.In_2, Part2.D7
  N12: IC2.+Vmotor, Motor_Power_Source.-
  N13: IC2.0V, Part2.GND, Motor_Power_Source.+
  N14: IC2.+V, Part2.VCC
  N15: IC3.Enable_1, Part3.D9_PWM
  N16: IC3.In_1, Part3.D8, U2.1A
  N17: IC3.Out_1_(_Controlled_by_Enable_1_), M2.pin_1
  N18: IC3.Out_2_(_Controlled_by_Enable_1_), M2.pin_2
  N19: IC3.In_2, U2.1Y
  N20: IC3.+Vmotor, Motor_Power_Source1.-
  GND: IC3.0V, Part3.GND, Motor_Power_Source1.+, U2.GND
  VCC: IC3.+V, Part3.VCC, U2.VCC
